# Fritzing sketch schematic (saved by Fritzing 0.9.3b)

parts:
  Part1 = Arduino Pro Mini (3.3V)
  Part2 = FTDI Basic Programmer
  C1 = Capacitor [package=cap-pth-small2]
  M1 = DC Motor
  U1 = POT [package=alps_pot]
  RE1 = Rotary Encoder [package=THT]
  R1 = Resistor [tolerance=±5% resistance=220 package=THT]
  R2 = Resistor [tolerance=±5% resistance=220 package=THT]
  Q1 = npn-Powertransistor [package="TO220 [THT]"]
  R3 = Resistor [tolerance=±5% resistance=220 package=THT]

nets:
  GND: Part1.GND, Part2.GND, U1.A, RE1.EncoderPinC, Q1.emitter
  N1: Part1.RESET, C1.2
  N2: Part1.VCC, Part2.POWER, M1.pin_1, U1.E, R1.Pin_0, R2.Pin_0
  N3: Part1.A1, U1.S
  N4: Part1.D9, R3.Pin_0
  N5: Part1.D4, RE1.EncoderPinB, R2.Pin_1
  N6: Part1.D3, RE1.EncoderPinA, R1.Pin_1
  N7: Part1.RXI, Part2.TXO
  N8: Part1.TXO, Part2.RXI
  N9: Part2.CTS, C1.1
  N10: M1.pin_2, Q1.collector
  N11: Q1.base, R3.Pin_1
